# Fritzing sketch fritzing-sketch (saved by Fritzing 0.9.3b)
breadboards: 1

parts:
  U1 = ESP32S-HiLetgo [part_number=ESP32S-HiLetgo]
  OLED2 = OLED Mono 0.56 inch blue or white  # not connected
  Part1 = Adafruit MAX9814 Electret Microphone Amplifier [part_number="Adafruit #1713"]

nets:
  N1: U1.3.3, Part1.VDD
  N2: U1.GPIO35, Part1.OUTPUT
  GND: U1.GND, Part1.GND

notes:
  Library: ggwave
  Example: esp32-rx
  Sample sketch for receiving sound data with ESP32.
  The OLED display is optional.
  Compatible microphones:
  - MAX9814
  - KY-037
  - KY-038
  - WS Sound Sensor

custom parts:
  ESP32S-HiLetgo: HiLetgo ESP-WROOM-32 ESP32 ESP-32S Development Board 2.4GHz Dual-Mode WiFi + Bluetooth Dual Cores Microcontroller The ESP32 integrated with Antenna switches, RF Balun, power amplifiers, low-noise amplifiers, filters, and management modules, and the entire solution occupies the least area of PCB. 2.4 GHz Wi-Fi plus Bluetooth dual-mode chip, with TSMC Ultra-low power consumption 40nm technology,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
  OLED Mono 0.56 inch blue or white: OLED, I2C 3.3V - 5V Blue and White text versions
  Adafruit MAX9814 Electret Microphone Amplifier: Add an ear to your project with this well-designed electret microphone amplifier with AGC. This fully assembled and tested board comes with a 20-20KHz electret microphone soldered on. For the amplification, we use the Maxim MAX9814, a specialty chip that is designed for amplifying electret microphones in situations where the loudness of the audio isn't predictable. This fancy microphone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
